# Fritzing sketch sketch (saved by Fritzing 0.9.3b)
breadboards: 1

parts:
  Composant3 = Seeeduino V3.0
  Composant4 = Seeeduino V3.0  # not connected
  Composant6 = INA219 High Side DC Current Sensor Breakout [part_number=904]
  U1 = Battery Holders [package=lipo-1100mAh]

nets:
  5V: Composant3.5V, Composant6.VCC
  GND: Composant3.GND, Composant6.GND, U1.-
  N1: Composant3.A4, Composant6.SDA
  N2: Composant3.A5, Composant3.SCL, Composant6.SCL
  N3: Composant6.VIN+, U1.+

notes:
  LIPO_BAT port
  Connecté à l'USB
  Cette plaque Arduino a sa consommation mesurée par l'autre. Elle pourrait avoir n'importe quelle configuration
  Le multimètre INA219 doit être branché en série à la sortie "+" de la batterie. Sa pin GND doit être partagée avec le pôle "-" de la batterie et la pin GND du Arduino de mesure

custom parts:
  INA219 High Side DC Current Sensor Breakout: This breakout board will solve all your power-monitoring problems. Instead of struggling with two multimeters, you can just use the handy INA219B chip on this breakout to both measure both the high side voltage and DC current draw over I2C with 1% precision. Most current-measuring devices such as our current panel meter are only good for low side measuring. That means that unless you want to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
